// Logisim project additionneur_8_bit_et_additionneur_soustracteur_8_bit_Lou_Eouzan.circ as structural Verilog: 4 circuits, main circuit additionneur_8_bit
module additionneur_8_bit (
  input  in_1,
  input  in_2,
  input  in_3,
  input  in_4,
  input  in_5,
  input  in_6,
  input  in_7,
  input  in_8,
  input  in_9,
  input  in_10,
  input  in_11,
  input  in_12,
  input  in_13,
  input  in_14,
  input  in_15,
  input  in_16,
  output out_17,
  output out_18,
  output out_19,
  output out_20,
  output out_21,
  output out_22,
  output out_23,
  output out_24,
  output out_25
);

  wire additionneur_1_reste, additionneur_2_reste, additionneur_3_reste, additionneur_4_reste,
       additionneur_5_reste, additionneur_6_reste, additionneur_7_reste;

  additionneur additionneur_1 (.in_1(in_8), .in_2(in_16), .in_3(1'b0), .reste(additionneur_1_reste), .somme(out_25));
  additionneur additionneur_2 (
    .in_1(in_7), .in_2(in_15), .in_3(additionneur_1_reste), .reste(additionneur_2_reste), .somme(out_24));
  additionneur additionneur_3 (
    .in_1(in_6), .in_2(in_14), .in_3(additionneur_2_reste), .reste(additionneur_3_reste), .somme(out_23));
  additionneur additionneur_4 (
    .in_1(in_5), .in_2(in_13), .in_3(additionneur_3_reste), .reste(additionneur_4_reste), .somme(out_22));
  additionneur additionneur_5 (
    .in_1(in_4), .in_2(in_12), .in_3(additionneur_4_reste), .reste(additionneur_5_reste), .somme(out_21));
  additionneur additionneur_6 (
    .in_1(in_3), .in_2(in_11), .in_3(additionneur_5_reste), .reste(additionneur_6_reste), .somme(out_20));
  additionneur additionneur_7 (
    .in_1(in_2), .in_2(in_10), .in_3(additionneur_6_reste), .reste(additionneur_7_reste), .somme(out_19));
  additionneur additionneur_8 (.in_1(in_1), .in_2(in_9), .in_3(additionneur_7_reste), .reste(out_17), .somme(out_18));
endmodule

module additionneur_soustracteur_8_bit (
  input  in_1,
  input  in_2,
  input  in_3,
  input  in_4,
  input  in_5,
  input  in_6,
  input  in_7,
  input  in_8,
  input  in_9,
  input  in_10,
  input  in_11,
  input  in_12,
  input  in_13,
  input  in_14,
  input  in_15,
  input  in_16,
  output out_17,
  output out_18,
  output out_19,
  output out_20,
  output out_21,
  output out_22,
  output out_23,
  output out_24,
  output out_25,
  output out_26
);

  wire additionneur_1_reste, additionneur_1_somme, additionneur_2_reste, additionneur_3_reste,
       additionneur_3_somme, additionneur_4_reste, additionneur_5_reste, additionneur_5_somme,
       additionneur_6_reste, additionneur_7_reste, additionneur_7_somme, additionneur_8_reste,
       additionneur_9_reste, additionneur_9_somme, additionneur_10_reste, additionneur_11_reste,
       additionneur_11_somme, additionneur_12_reste, additionneur_13_reste, additionneur_13_somme,
       additionneur_14_reste, additionneur_15_somme, not_1_out, not_2_out, not_3_out, not_4_out, not_5_out,
       not_6_out, not_7_out, not_8_out;

  not not_1 (not_1_out, in_9);
  not not_2 (not_2_out, in_10);
  not not_3 (not_3_out, in_11);
  not not_4 (not_4_out, in_12);
  not not_5 (not_5_out, in_13);
  not not_6 (not_6_out, in_14);
  not not_7 (not_7_out, in_15);
  not not_8 (not_8_out, in_16);
  additionneur additionneur_1 (
    .in_1(not_8_out), .in_2(1'b1), .in_3(1'b0), .reste(additionneur_1_reste), .somme(additionneur_1_somme));
  additionneur additionneur_2 (
    .in_1(in_8), .in_2(additionneur_1_somme), .in_3(1'b0), .reste(additionneur_2_reste), .somme(out_26));
  additionneur additionneur_3 (
    .in_1(not_7_out), .in_2(1'b0), .in_3(additionneur_1_reste), .reste(additionneur_3_reste),
    .somme(additionneur_3_somme));
  additionneur additionneur_4 (
    .in_1(in_7), .in_2(additionneur_3_somme), .in_3(additionneur_2_reste), .reste(additionneur_4_reste),
    .somme(out_25));
  additionneur additionneur_5 (
    .in_1(not_6_out), .in_2(1'b0), .in_3(additionneur_3_reste), .reste(additionneur_5_reste),
    .somme(additionneur_5_somme));
  additionneur additionneur_6 (
    .in_1(in_6), .in_2(additionneur_5_somme), .in_3(additionneur_4_reste), .reste(additionneur_6_reste),
    .somme(out_24));
  additionneur additionneur_7 (
    .in_1(not_5_out), .in_2(1'b0), .in_3(additionneur_5_reste), .reste(additionneur_7_reste),
    .somme(additionneur_7_somme));
  additionneur additionneur_8 (
    .in_1(in_5), .in_2(additionneur_7_somme), .in_3(additionneur_6_reste), .reste(additionneur_8_reste),
    .somme(out_23));
  additionneur additionneur_9 (
    .in_1(not_4_out), .in_2(1'b0), .in_3(additionneur_7_reste), .reste(additionneur_9_reste),
    .somme(additionneur_9_somme));
  additionneur additionneur_10 (
    .in_1(in_4), .in_2(additionneur_9_somme), .in_3(additionneur_8_reste), .reste(additionneur_10_reste),
    .somme(out_22));
  additionneur additionneur_11 (
    .in_1(not_3_out), .in_2(1'b0), .in_3(additionneur_9_reste), .reste(additionneur_11_reste),
    .somme(additionneur_11_somme));
  additionneur additionneur_12 (
    .in_1(in_3), .in_2(additionneur_11_somme), .in_3(additionneur_10_reste), .reste(additionneur_12_reste),
    .somme(out_21));
  additionneur additionneur_13 (
    .in_1(not_2_out), .in_2(1'b0), .in_3(additionneur_11_reste), .reste(additionneur_13_reste),
    .somme(additionneur_13_somme));
  additionneur additionneur_14 (
    .in_1(in_2), .in_2(additionneur_13_somme), .in_3(additionneur_12_reste), .reste(additionneur_14_reste),
    .somme(out_20));
  additionneur additionneur_15 (
    .in_1(not_1_out), .in_2(1'b0), .in_3(additionneur_13_reste), .reste(out_17), .somme(additionneur_15_somme));
  additionneur additionneur_16 (
    .in_1(in_1), .in_2(additionneur_15_somme), .in_3(additionneur_14_reste), .reste(out_18), .somme(out_19));
endmodule

module demi_additionneur (
  input  in_1,
  input  in_2,
  output reste,
  output somme
);

  wire not_1_out, or_1_out;

  and and_1 (reste, in_1, in_2);
  or or_1 (or_1_out, in_1, in_2);
  not not_1 (not_1_out, reste);
  and and_2 (somme, not_1_out, or_1_out);
endmodule

module additionneur (
  input  in_1,
  input  in_2,
  input  in_3,
  output reste,
  output somme
);

  wire demi_additionneur_1_reste, demi_additionneur_1_somme, demi_additionneur_2_reste;

  demi_additionneur demi_additionneur_1 (
    .in_1(in_1), .in_2(in_2), .reste(demi_additionneur_1_reste), .somme(demi_additionneur_1_somme));
  demi_additionneur demi_additionneur_2 (
    .in_1(demi_additionneur_1_somme), .in_2(in_3), .reste(demi_additionneur_2_reste), .somme(somme));
  or or_1 (reste, demi_additionneur_1_reste, demi_additionneur_2_reste);
endmodule
