// Logisim project prise_en_main_tp_Lou_Eouzan.circ as structural Verilog: 1 circuit, main circuit prise_en_main_logisim
module prise_en_main_logisim (
  input  c,
  input  b,
  input  a,
  output s
);

  wire and_1_out, not_1_out;

  not not_1 (not_1_out, c);
  and and_1 (and_1_out, not_1_out, b);
  or or_1 (s, and_1_out, a);
endmodule
