// Logisim project s1_s2_s3_Lou_Eouzan.circ as structural Verilog: 3 circuits, main circuit circuit_S1
module circuit_S1 (
  input  a,
  input  b,
  input  c,
  input  d,
  output s1
);

  wire and_1_out, and_2_out, and_3_out, and_4_out, and_5_out, and_6_out, and_7_out, and_8_out, not_1_out,
       not_2_out, not_3_out, not_4_out, or_1_out, or_2_out, or_3_out;

  not not_1 (not_1_out, a);
  not not_2 (not_2_out, b);
  not not_3 (not_3_out, c);
  not not_4 (not_4_out, d);
  and and_1 (and_1_out, not_2_out, not_4_out);
  and and_2 (and_2_out, c, d);
  and and_3 (and_3_out, c, not_4_out);
  and and_4 (and_4_out, not_3_out, d);
  or or_1 (or_1_out, and_1_out, and_2_out);
  or or_2 (or_2_out, and_3_out, and_4_out);
  and and_5 (and_5_out, b, or_2_out);
  and and_6 (and_6_out, a, not_2_out);
  or or_3 (or_3_out, or_1_out, and_5_out);
  and and_7 (and_7_out, and_6_out, not_3_out);
  and and_8 (and_8_out, not_1_out, or_3_out);
  or or_4 (s1, and_7_out, and_8_out);
endmodule

module circuit_s2 (
  input  a,
  input  b,
  input  c,
  input  d,
  output s2
);

  wire and_1_out, and_2_out, and_3_out, and_4_out, and_5_out, and_6_out, and_7_out, and_8_out, and_9_out,
       and_10_out, and_11_out, not_1_out, not_2_out, not_3_out, not_4_out, or_1_out, or_2_out, or_3_out,
       or_4_out;

  not not_1 (not_1_out, a);
  not not_2 (not_2_out, b);
  not not_3 (not_3_out, c);
  not not_4 (not_4_out, d);
  and and_1 (and_1_out, not_1_out, not_2_out);
  and and_2 (and_2_out, not_1_out, b);
  and and_3 (and_3_out, a, not_2_out);
  and and_4 (and_4_out, not_1_out, b);
  and and_5 (and_5_out, a, not_2_out);
  and and_6 (and_6_out, not_1_out, b);
  or or_1 (or_1_out, and_1_out, and_2_out);
  or or_2 (or_2_out, and_4_out, and_5_out);
  and and_7 (and_7_out, and_6_out, c);
  or or_3 (or_3_out, or_1_out, and_3_out);
  and and_8 (and_8_out, or_3_out, not_4_out);
  and and_9 (and_9_out, d, or_2_out);
  and and_10 (and_10_out, and_7_out, d);
  or or_4 (or_4_out, and_8_out, and_9_out);
  and and_11 (and_11_out, or_4_out, not_3_out);
  or or_5 (s2, and_11_out, and_10_out);
endmodule

module circuit_s3 (
  input  a,
  input  b,
  input  c,
  input  d,
  output s3
);

  wire and_1_out, and_2_out, and_3_out, and_4_out, and_5_out, and_6_out, and_7_out, and_8_out, and_9_out,
       and_10_out, and_11_out, and_12_out, and_13_out, and_14_out, and_15_out, and_16_out, and_17_out,
       not_1_out, not_2_out, not_3_out, not_4_out, or_1_out, or_2_out, or_3_out, or_4_out, or_5_out, or_6_out;

  not not_1 (not_1_out, a);
  not not_2 (not_2_out, b);
  not not_3 (not_3_out, c);
  not not_4 (not_4_out, d);
  and and_1 (and_1_out, not_2_out, not_3_out);
  and and_2 (and_2_out, and_1_out, not_4_out);
  or or_1 (or_1_out, and_5_out, and_2_out);
  and and_3 (and_3_out, not_2_out, not_3_out);
  and and_4 (and_4_out, a, not_2_out);
  and and_5 (and_5_out, and_3_out, d);
  and and_6 (and_6_out, not_2_out, c);
  and and_7 (and_7_out, and_4_out, not_3_out);
  and and_8 (and_8_out, and_6_out, not_4_out);
  or or_2 (or_2_out, or_1_out, and_8_out);
  and and_9 (and_9_out, not_2_out, c);
  and and_10 (and_10_out, and_9_out, d);
  or or_3 (or_3_out, or_2_out, and_10_out);
  and and_11 (and_11_out, b, not_3_out);
  or or_4 (or_4_out, or_3_out, and_12_out);
  and and_12 (and_12_out, and_11_out, not_4_out);
  and and_13 (and_13_out, b, c);
  and and_14 (and_14_out, and_13_out, not_4_out);
  or or_5 (or_5_out, or_4_out, and_14_out);
  and and_15 (and_15_out, b, c);
  and and_16 (and_16_out, and_15_out, d);
  or or_6 (or_6_out, or_5_out, and_16_out);
  or or_7 (s3, and_7_out, and_17_out);
  and and_17 (and_17_out, not_1_out, or_6_out);
endmodule
